// Logisim project LabArqui.circ as structural Verilog
module OneBitComparator (
  input  A,
  input  B,
  output AGB,
  output ALB,
  output AEB
);

  wire not_1_out, not_2_out, or_1_out;

  not not_1 (not_1_out, B);
  not not_2 (not_2_out, A);
  and and_1 (AGB, A, not_1_out);
  and and_2 (ALB, not_2_out, B);
  or or_1 (or_1_out, ALB, AGB);
  not not_3 (AEB, or_1_out);

  // Notes on the sheet:
  //   A>B
  //   A<B
  //   A=B
endmodule

module TwoBitComparator (
  input  A1,
  input  A0,
  input  B1,
  input  B0,
  output AGB,
  output ALB,
  output AEB
);

  wire and_1_out, and_2_out, onebitcomparator_1_aeb, onebitcomparator_1_agb, onebitcomparator_1_alb,
       onebitcomparator_2_aeb, onebitcomparator_2_agb, onebitcomparator_2_alb;

  OneBitComparator onebitcomparator_1 (
    .A(A1), .B(B1), .AGB(onebitcomparator_1_agb), .ALB(onebitcomparator_1_alb), .AEB(onebitcomparator_1_aeb));
  OneBitComparator onebitcomparator_2 (
    .A(A0), .B(B0), .AGB(onebitcomparator_2_agb), .ALB(onebitcomparator_2_alb), .AEB(onebitcomparator_2_aeb));
  and and_1 (and_1_out, onebitcomparator_1_aeb, onebitcomparator_2_agb);
  and and_2 (and_2_out, onebitcomparator_2_alb, onebitcomparator_1_aeb);
  or or_1 (AGB, onebitcomparator_1_agb, and_1_out);
  or or_2 (ALB, onebitcomparator_1_alb, and_2_out);
  and and_3 (AEB, onebitcomparator_1_aeb, onebitcomparator_2_aeb);

  // Notes on the sheet:
  //   +SBIT
  //   -SBIT
endmodule
